# Fritzing sketch kinowheels_receiver_sbus (saved by Fritzing 0.9.6b)
breadboards: 1
perfboards: 2

parts:
  Composant5 = Arduino Nano (Rev3.0)
  IC2 = Hex Inverter Schmitt Trigger SN74HC14 [package="DIP (Dual Inline)"]
  Composant6 = NRF24L01+ Breakout Board  # not connected
  U13 = Nokia 6100 Color LCD [package=nokia6100_lcd]
  SW4 = ENCODER_RGB_CA [package=encoder_led_3]

nets:
  N1: Composant5.D1/TX, IC2.6A
  GND: Composant5.GND, IC2.GND, U13.CS, SW4.C
  N2: Composant5.D2, SW4.-B
  N3: Composant5.D4, SW4.+
  N4: Composant5.D6, SW4.A
  VIN: Composant5.VIN, IC2.VCC, U13.SCK, SW4.B
  N5: Composant5.A5, U13.DIO
  N6: Composant5.A4, U13.RESET

notes:
  GND / VCC / SCL / SDA
  SBUS RONIN
  noir = ground
  marron sur RX ronin
  FUTABA cable
  GND / + / SW / DT / CLK
  CE
  CSN
  SCK
  MO
  M
