# Fritzing sketch kinowheels_transmitter_due (saved by Fritzing 0.9.6b)
perfboards: 1
stripboards: 6
breadboards: 4

parts:
  Composant4 = NRF24L01+ Breakout Board  # not connected
  Composant7 = Arduino Due (Rev2b)
  U11 = Nokia 6100 Color LCD [package=nokia6100_lcd]
  VCC1 = Battery block 9V
  M2 = RioRand LM2596
  R14 = Resistor [tolerance=±5% power=0.25 resistance=10 package=THT]
  R15 = Resistor [tolerance=±5% power=0.25 resistance=10 package=THT]
  R16 = Resistor [tolerance=±5% power=0.25 resistance=10 package=THT]
  R17 = Resistor [tolerance=±5% power=0.25 resistance=10 package=THT]
  S3 = Pushbutton [package=THT]
  R18 = Rotary Potentiometer (Small) [maximum_resistance=100kΩ package=THT]
  JP1 = Header 4 [package=jst-4-pth]
  R19 = Resistor [tolerance=±5% power=0.25 resistance=10 package=THT]
  S4 = Pushbutton [package=THT]
  R20 = Rotary Potentiometer (Small) [maximum_resistance=100kΩ package=THT]
  R21 = Resistor [tolerance=±5% power=0.25 resistance=10 package=THT]
  R22 = Resistor [tolerance=±5% power=0.25 resistance=10 package=THT]
  R23 = Resistor [tolerance=±5% power=0.25 resistance=10 package=THT]
  R24 = Resistor [tolerance=±5% power=0.25 resistance=10 package=THT]
  R25 = Resistor [tolerance=±5% power=0.25 resistance=10 package=THT]
  JP2 = Header 4 [package=jst-4-pth]
  S5 = Pushbutton [package=THT]
  R26 = Rotary Potentiometer (Small) [maximum_resistance=100kΩ package=THT]
  R27 = Resistor [tolerance=±5% power=0.25 resistance=10 package=THT]
  R28 = Resistor [tolerance=±5% power=0.25 resistance=10 package=THT]
  R29 = Resistor [tolerance=±5% power=0.25 resistance=10 package=THT]
  R30 = Resistor [tolerance=±5% power=0.25 resistance=10 package=THT]
  R31 = Resistor [tolerance=±5% power=0.25 resistance=10 package=THT]
  JP3 = Header 4 [package=jst-4-pth]
  IC3 = Hex Inverter Schmitt Trigger SN74HC14 [package="DIP (Dual Inline)"]
  JP4 = Header 4 [package=jst-4-pth]
  U12 = SWITCH_SPDT [package=kps-1290]
  SW3 = ENCODER_RGB_CA [package=encoder_led_3]

nets:
  N1: Composant7.A1, R26.wiper
  N2: Composant7.A2, R20.wiper
  N3: Composant7.A3, R18.wiper
  N4: Composant7.D14/TX3, IC3.6A
  N5: Composant7.D18/TX1, R25.Pin_0
  N6: Composant7.D19/RX1, R22.Pin_0, R23.Pin_1, JP2.4
  N7: Composant7.D20/SDA3, U11.RESET
  N8: Composant7.D21/SCL3, U11.DIO
  N9: Composant7.IOREF, U11.SCK, R15.Pin_1, R16.Pin_0, S3.leg0, R18.leg2, JP1.2, S4.leg0, R20.leg2, R23.Pin_0, R24.Pin_1, JP2.2, S5.leg0, R26.leg2, R29.Pin_0, R30.Pin_1, JP3.2, SW3.B
  5V: Composant7.5V, IC3.VCC
  GND: Composant7.GND, U11.CS, M2.Pin_4, R18.leg1, JP1.1, R19.Pin_0, R20.leg1, R21.Pin_0, JP2.1, R26.leg1, R27.Pin_0, JP3.1, IC3.GND, JP4.3, SW3.C
  N10: Composant7.VIN, M2.Pin_3
  N11: Composant7.D9_PWM, SW3.A
  N12: Composant7.D10_PWM/SS0, SW3.-B
  N13: Composant7.D11_PWM, SW3.+
  N14: Composant7.D2_PWM, R28.Pin_1
  N15: Composant7.D3_PWM, R31.Pin_0
  N16: Composant7.D4_PWM/SS1, S3.leg1, R19.Pin_1
  N17: Composant7.D5_PWM, S4.leg1, R21.Pin_1
  N18: Composant7.D6_PWM, S5.leg1, R27.Pin_1
  N19: Composant7.D22, R14.Pin_0
  N20: Composant7.D23, R17.Pin_1
  N21: VCC1.-, U12.S
  N22: VCC1.+, M2.Pin_1
  N23: M2.Pin_2, U12.O
  N24: R14.Pin_1, R15.Pin_0, JP1.3
  N25: R16.Pin_1, R17.Pin_0, JP1.4
  N26: R24.Pin_0, R25.Pin_1, JP2.3
  N27: R28.Pin_0, R29.Pin_1, JP3.4
  N28: R30.Pin_0, R31.Pin_1, JP3.3
  N29: IC3.6Y, JP4.1

notes:
  PAN
  TILT
  SBUS RONIN
  noir = ground
  marron sur RX ronin
  GND / VCC / SCL / SDA
  SORTIE 7v
  ROLL
  3V3
  5V
  3v 3
  FUTABA cable
  GND / + / SW / DT / CLK
  CE
  CSN
  SCK
  MO
  M
