# Fritzing sketch sbus_receiver_debug_lcd (saved by Fritzing 0.9.6b)
perfboards: 1

parts:
  Composant1 = Arduino Uno (Rev3) - ICSP
  IC3 = Hex Inverter Schmitt Trigger SN74HC14 [package="DIP (Dual Inline)"]  # not connected
  U12 = Nokia 6100 Color LCD [package=nokia6100_lcd]
  JP5 = Header 4 [package=jst-4-pth]  # not connected

nets:
  N1: Composant1.A4/SDA, U12.RESET
  N2: Composant1.A5/SCL, U12.DIO
  N3: Composant1.5V, U12.SCK
  N4: Composant1.GND, U12.CS

notes:
  GND / VCC / SCL / SDA
  SBUS RONIN
  noir = ground
  Bleu sur RX ronin
  FUTABA
